# Fritzing sketch Schaltplan smart riders_mit_Kamera (saved by Fritzing 0.9.10b)
breadboards: 1

parts:
  motortreiber = L298 [package=multiwatt15]
  Step-Up_13_5_V_stromversorgung_motor = Boost Convertor [part_number=XL6009E1 package=THT]
  Step-Down5V_für_Arduino_LCD_display_Servo = RioRand LM2596
  11_1_V_lipo = LIPO-2000mAh [package=lipo-2000]
  Lenkservo = Basic Servo
  Ein/Aus_Schalter = Reed switch [package=THT]
  Bauteil1 = Arduino Nano (Rev3.0) (ICSP)
  Rechts = HC-SR04 Ultrasonic Distance Sensor
  Mitte = HC-SR04 Ultrasonic Distance Sensor
  Links = HC-SR04 Ultrasonic Distance Sensor
  Bauteil2 = 9-DOF Absolute Orientation IMU Fusion Breakout - BNO055
  LCD_Display_3-farbig = LCD1602-I2C
  M1 = DC Motor [voltage_(max)=6V voltage_(min)=3V]
  startbutton = Round Pushbutton
  R1 = Resistor [tolerance=±5% resistance=1k package="1206 [SMD]"]
  Pixycam_2_1 = HuskyLens-Vision-Sensor_1

nets:
  N1: motortreiber.OUT1, M1.pin_1
  N2: motortreiber.OUT2, M1.pin_2
  N3: motortreiber.VS, Step-Up_13_5_V_stromversorgung_motor.Positive_Output
  N4: motortreiber.IN1, Bauteil1.D6
  N5: motortreiber.ENA, Bauteil1.D5
  N6: motortreiber.IN2, Bauteil1.D7
  GND: motortreiber.GND, Step-Up_13_5_V_stromversorgung_motor.Negative_Output, Step-Down5V_für_Arduino_LCD_display_Servo.Pin_4, Lenkservo.gnd, Bauteil1.GND, Rechts.GND, Mitte.GND, Links.GND, Bauteil2.GND, LCD_Display_3-farbig.GND, R1.Pin_1, Pixycam_2_1.pin3
  VCC: motortreiber.VLS, Bauteil1.5V, Rechts.VCC, Mitte.VCC, Links.VCC, Bauteil2.5.0V, startbutton.leg0, Pixycam_2_1.pin4
  N7: Step-Up_13_5_V_stromversorgung_motor.Negative_Input, Step-Down5V_für_Arduino_LCD_display_Servo.Pin_2, 11_1_V_lipo.-
  N8: Step-Up_13_5_V_stromversorgung_motor.Positive_Input, Step-Down5V_für_Arduino_LCD_display_Servo.Pin_1, Ein/Aus_Schalter.pin_1
  VCC_2: Step-Down5V_für_Arduino_LCD_display_Servo.Pin_3, Lenkservo.vcc, Bauteil1.VIN, LCD_Display_3-farbig.VCC
  N9: 11_1_V_lipo.+, Ein/Aus_Schalter.pin_2
  N10: Lenkservo.pulse, Bauteil1.D3
  N11: Bauteil1.D4, startbutton.leg1, R1.Pin_0
  N12: Bauteil1.D8, Mitte.TRIG
  N13: Bauteil1.D9, Mitte.ECHO
  N14: Bauteil1.D11/MOSI, Pixycam_2_1.pin1
  N15: Bauteil1.D12/MISO, Pixycam_2_1.pin2
  N16: Bauteil1.A5, Bauteil2.SCL_5V, LCD_Display_3-farbig.SCL
  N17: Bauteil1.A4, Bauteil2.SDA_5V, LCD_Display_3-farbig.SDA
  N18: Bauteil1.A3, Rechts.ECHO
  N19: Bauteil1.A2, Rechts.TRIG
  N20: Bauteil1.A1, Links.ECHO
  N21: Bauteil1.A0, Links.TRIG

notes:
  Ultraschall sensoren
  Stromversorgung
  kamera

custom parts:
  Boost Convertor: DC to DC boost convertor
  9-DOF Absolute Orientation IMU Fusion Breakout - BNO055: A MEMS accelerometer, magnetometer and gyroscope on a single die with a high speed ARM Cortex-M0 based processor to digest all the sensor data, abstract the sensor fusion and real time requirements away, and spit out data you can use in quaternions, Euler angles or vectors.
  LCD1602-I2C: A standard character display, usually with 2x16 characters. Comes in many colors with LCM1602 IIC attached.
  HuskyLens-Vision-Sensor_1: Huskylens is an easy-to-use AI Camera | Vision Sensor. DFrobot Huskylens is equipped with multiple functions, such as face recognition, object tracking, object recognition, line tracking, color recognition, and tag(QR code) recognition.
